# Fritzing sketch Wemos_MHZ19B_BME280 (saved by Fritzing 0.9.4)
breadboards: 1

parts:
  WeMos_D1_Mini_WS2812B_RGB_Shield1 = WeMos D1 Mini WS2812B RGB Shield
  TD-er1 = MH-Z19 CO2 sensor [part_number=MH-Z19]
  Componente1 = BME280 Breakout
  R1 = Resistor [tolerance=±5% resistance=220 package=THT]
  R2 = Resistor [tolerance=±5% resistance=220 package=THT]
  R3 = Resistor [tolerance=±5% resistance=220 package=THT]
  LED1 = LED - 5mm [color="Red (633nm)" package="5 mm [THT]"]
  LED2 = LED - 5mm [color="Orange (620nm)" package="5 mm [THT]"]
  LED3 = LED - 5mm [color="Green (570nm)" package="5 mm [THT]"]

nets:
  3V3: WeMos_D1_Mini_WS2812B_RGB_Shield1.3V3, Componente1.3.3V
  5V: WeMos_D1_Mini_WS2812B_RGB_Shield1.5V, TD-er1.Vin, LED1.cathode, LED2.cathode, LED3.cathode
  N1: WeMos_D1_Mini_WS2812B_RGB_Shield1.D1, Componente1.SCK/SCL
  N2: WeMos_D1_Mini_WS2812B_RGB_Shield1.D2, Componente1.SDI/SDA
  N3: WeMos_D1_Mini_WS2812B_RGB_Shield1.D4, R3.Pin_1
  N4: WeMos_D1_Mini_WS2812B_RGB_Shield1.D5, R2.Pin_1
  N5: WeMos_D1_Mini_WS2812B_RGB_Shield1.D6, R1.Pin_1
  GND: WeMos_D1_Mini_WS2812B_RGB_Shield1.G, TD-er1.GND, Componente1.GND
  N6: R1.Pin_0, LED1.anode
  N7: R2.Pin_0, LED2.anode
  N8: R3.Pin_0, LED3.anode
